// Logisim project datapath.circ as structural Verilog: 8 circuits, main circuit Datapath
module Datapath (
  input  [31:0] Q,
  input  sM,
  input  [31:0] M,
  input  L_Q,
  input  clk,
  input  L_M,
  input  clr,
  input  L_P,
  input  count,
  input  Res_Clr,
  input  ALU,
  output [31:0] M_2,
  output [31:0] P,
  output lsb,
  output carry,
  output END
);

  wire [31:0] alu_1_left_half_p, alu_1_right_half_p, counter_1_q, multiplexer_1_out, Q_q;

  Register #(.width(32)) u_Q (.D(Q), .en(L_Q), .Q(Q_q), .clk(clk), .clr(clr));
  ALU alu_1 (
    .M_cand(Q_q), .Product(P), .M_lier({M_2[31:1], lsb}), .Left_Half_P(alu_1_left_half_p),
    .Right_Half_P(alu_1_right_half_p), .selALU(ALU), .Carry(carry));
  Register #(.width(32)) u_M (.D(multiplexer_1_out), .en(L_M), .Q({M_2[31:1], lsb}), .clk(clk), .clr(clr));
  Register #(.width(32)) u_P (.D(alu_1_left_half_p), .en(L_P), .Q(P), .clk(clk), .clr(clr));
  Multiplexer #(.width(32)) multiplexer_1 (
    .in0(M), .in1(alu_1_right_half_p), .out(multiplexer_1_out), .sel(sM));  // open: en
  Counter #(.width(32), .max('h1f), .ongoal("stay")) counter_1 (
    .count(count), .Q(counter_1_q), .clk(clk), .clr(Res_Clr));  // open: load, D, carry
  // Probe on counter_1_q
  // Probe on 32'h1f
  Comparator comparator_1 (.X(counter_1_q), .Y(32'h1f), .OUT(END));

  assign M_2[0] = lsb;

  // Notes on the sheet:
  //   =================================================================================================================================================================
  //   =================================================================================================================================================================
  //   Constant "31" check for counter..
  //   If count == 31 then exit
endmodule

module ALU (
  input  [31:0] M_cand,
  input  [31:0] Product,
  input  [31:0] M_lier,
  input  selALU,
  output Carry,
  output [31:0] Left_Half_P,
  output [31:0] Right_Half_P
);

  wire [31:0] n32_bit_adder_1_sum, shifter_1_mult_out, shifter_1_product_out;

  // Probe on M_cand
  // Probe on Product
  // Probe on M_lier
  _32_Bit_Adder u_32_bit_adder_1 (.A(M_cand), .B(Product), .SUM(n32_bit_adder_1_sum), .C_In(1'b0), .C_Out(Carry));
  Shifter shifter_1 (
    .Product_In(Product), .Multiplier_In(M_lier), .Product_Out(shifter_1_product_out),
    .Mult_Out(shifter_1_mult_out));
  // Probe on n32_bit_adder_1_sum
  // Probe on shifter_1_product_out
  // Probe on Left_Half_P
  Multiplexer #(.width(32)) multiplexer_1 (
    .in0(n32_bit_adder_1_sum), .in1(shifter_1_product_out), .out(Left_Half_P), .sel(selALU));  // open: en
  Multiplexer #(.width(32)) multiplexer_2 (
    .in0(M_lier), .in1(shifter_1_mult_out), .out(Right_Half_P), .sel(selALU));  // open: en
  // Probe on Right_Half_P

  // Notes on the sheet:
  //   Shifter = selALU(1)
endmodule

module Shifter (
  input  [31:0] Product_In,
  input  [31:0] Multiplier_In,
  output [31:0] Product_Out,
  output [31:0] Mult_Out
);


  assign Mult_Out = {Product_In[0], Multiplier_In[31:1]};
  assign Product_Out = {1'b0, Product_In[31:1]};

  // Other names for the same wires on the sheet: In_M[31:0] = Multiplier_In; _31_0 = Product_In[0];
  //   In_P[31:0] = Product_In; Out_M[31:0] = {Product_In[0], Multiplier_In[31:1]}; Out_P[30:0] = Product_In[31:1]

  // Notes on the sheet:
  //   INPUTS
  //   Constant Zero that comes from shift.
  //   ==============================================================
  //   OUTPUTS
  //   This is the shift method
  //   Zero comes from MSB
endmodule

module _32_Bit_Adder (
  input  C_In,
  input  [31:0] A,
  input  [31:0] B,
  output [31:0] SUM,
  output C_Out
);

  wire n4_bit_adder_1_cout, n4_bit_adder_2_cout, n4_bit_adder_3_cout, n4_bit_adder_4_cout,
       n4_bit_adder_5_cout, n4_bit_adder_6_cout, n4_bit_adder_7_cout;

  // Probe on A
  // Probe on B
  _4_Bit_Adder u_4_bit_adder_1 (.in_2(A[3:0]), .in_3(B[3:0]), .out_4(SUM[3:0]), .Cin(C_In), .Cout(n4_bit_adder_1_cout));
  _4_Bit_Adder u_4_bit_adder_2 (
    .in_2(A[7:4]), .in_3(B[7:4]), .out_4(SUM[7:4]), .Cin(n4_bit_adder_1_cout), .Cout(n4_bit_adder_2_cout));
  _4_Bit_Adder u_4_bit_adder_3 (
    .in_2(A[11:8]), .in_3(B[11:8]), .out_4(SUM[11:8]), .Cin(n4_bit_adder_2_cout), .Cout(n4_bit_adder_3_cout));
  _4_Bit_Adder u_4_bit_adder_4 (
    .in_2(A[15:12]), .in_3(B[15:12]), .out_4(SUM[15:12]), .Cin(n4_bit_adder_3_cout),
    .Cout(n4_bit_adder_4_cout));
  _4_Bit_Adder u_4_bit_adder_5 (
    .in_2(A[19:16]), .in_3(B[19:16]), .out_4(SUM[19:16]), .Cin(n4_bit_adder_4_cout),
    .Cout(n4_bit_adder_5_cout));
  _4_Bit_Adder u_4_bit_adder_6 (
    .in_2(A[23:20]), .in_3(B[23:20]), .out_4(SUM[23:20]), .Cin(n4_bit_adder_5_cout),
    .Cout(n4_bit_adder_6_cout));
  _4_Bit_Adder u_4_bit_adder_7 (
    .in_2(A[27:24]), .in_3(B[27:24]), .out_4(SUM[27:24]), .Cin(n4_bit_adder_6_cout),
    .Cout(n4_bit_adder_7_cout));
  _4_Bit_Adder u_4_bit_adder_8 (
    .in_2(A[31:28]), .in_3(B[31:28]), .out_4(SUM[31:28]), .Cin(n4_bit_adder_7_cout), .Cout(C_Out));
  // Probe on SUM
endmodule

module Comparator (
  input  [31:0] X,
  input  [31:0] Y,
  output OUT
);

  wire n4_bit_equality_1_out_3, n4_bit_equality_2_out_3, n4_bit_equality_3_out_3, n4_bit_equality_4_out_3,
       n4_bit_equality_5_out_3, n4_bit_equality_6_out_3, n4_bit_equality_7_out_3, n4_bit_equality_8_out_3;

  // Probe on X
  // Probe on Y
  _4_Bit_Equality u_4_bit_equality_1 (.in_1(X[3:0]), .in_2(Y[3:0]), .out_3(n4_bit_equality_1_out_3));
  _4_Bit_Equality u_4_bit_equality_2 (.in_1(X[7:4]), .in_2(Y[7:4]), .out_3(n4_bit_equality_2_out_3));
  _4_Bit_Equality u_4_bit_equality_3 (.in_1(X[11:8]), .in_2(Y[11:8]), .out_3(n4_bit_equality_3_out_3));
  _4_Bit_Equality u_4_bit_equality_4 (.in_1(X[15:12]), .in_2(Y[15:12]), .out_3(n4_bit_equality_4_out_3));
  _4_Bit_Equality u_4_bit_equality_5 (.in_1(X[19:16]), .in_2(Y[19:16]), .out_3(n4_bit_equality_5_out_3));
  _4_Bit_Equality u_4_bit_equality_6 (.in_1(X[23:20]), .in_2(Y[23:20]), .out_3(n4_bit_equality_6_out_3));
  _4_Bit_Equality u_4_bit_equality_7 (.in_1(X[27:24]), .in_2(Y[27:24]), .out_3(n4_bit_equality_7_out_3));
  _4_Bit_Equality u_4_bit_equality_8 (.in_1(X[31:28]), .in_2(Y[31:28]), .out_3(n4_bit_equality_8_out_3));
  and and_1 (OUT, n4_bit_equality_1_out_3, n4_bit_equality_2_out_3, n4_bit_equality_3_out_3, n4_bit_equality_4_out_3, n4_bit_equality_5_out_3, n4_bit_equality_6_out_3, n4_bit_equality_7_out_3, n4_bit_equality_8_out_3);
endmodule

module _4_Bit_Equality (
  input  [3:0] in_1,
  input  [3:0] in_2,
  output out_3
);

  wire xnor_1_out, xnor_2_out, xnor_3_out, xnor_4_out;

  xnor xnor_1 (xnor_1_out, in_1[0], in_2[0]);
  xnor xnor_2 (xnor_2_out, in_1[1], in_2[1]);
  xnor xnor_3 (xnor_3_out, in_1[2], in_2[2]);
  xnor xnor_4 (xnor_4_out, in_1[3], in_2[3]);
  and and_1 (out_3, xnor_1_out, xnor_2_out, xnor_3_out, xnor_4_out);
endmodule

module _4_Bit_Adder (
  input  Cin,
  input  [3:0] in_2,
  input  [3:0] in_3,
  output [3:0] out_4,
  output Cout
);

  wire f_adder_1_carryout, f_adder_2_carryout, f_adder_3_carryout;

  F_Adder f_adder_1 (.in_2(in_2[0]), .in_3(in_3[0]), .Sum(out_4[0]), .carryIn(Cin), .carryOut(f_adder_1_carryout));
  F_Adder f_adder_2 (
    .in_2(in_2[1]), .in_3(in_3[1]), .Sum(out_4[1]), .carryIn(f_adder_1_carryout),
    .carryOut(f_adder_2_carryout));
  F_Adder f_adder_3 (
    .in_2(in_2[2]), .in_3(in_3[2]), .Sum(out_4[2]), .carryIn(f_adder_2_carryout),
    .carryOut(f_adder_3_carryout));
  F_Adder f_adder_4 (.in_2(in_2[3]), .in_3(in_3[3]), .Sum(out_4[3]), .carryIn(f_adder_3_carryout), .carryOut(Cout));
endmodule

module F_Adder (
  input  carryIn,
  input  in_2,
  input  in_3,
  output Sum,
  output carryOut
);

  wire and_1_out, and_2_out, xor_1_out;

  and and_1 (and_1_out, in_2, in_3);
  xor xor_1 (xor_1_out, in_2, in_3);
  or or_1 (carryOut, and_1_out, and_2_out);
  and and_2 (and_2_out, carryIn, xor_1_out);
  xor xor_2 (Sum, carryIn, xor_1_out);
endmodule
