// Logisim project mult32.circ as structural Verilog: 1 circuit, main circuit main
module main (
  input  [31:0] M_lier,
  input  [31:0] M_cand,
  output [31:0] Product_First_Half,
  output [31:0] M_lier_Second_Half,
  output Product_Carry
);

  wire button_1_out, CLK_out, control_1_alu, control_1_clr, control_1_count, control_1_l_m, control_1_l_p,
       control_1_l_q, control_1_res_clr, control_1_sm, datapath_1_end, datapath_1_lsb, xor_1_out;
  wire [2:0] control_1_states;

  Button button_1 (.out(button_1_out));
  // Probe on M_lier
  // Probe on M_cand
  xor xor_1 (xor_1_out, button_1_out, 1'b1);
  Clock CLK (.out(CLK_out));
  // Probe on Product_First_Half
  Control control_1 (
    .STATES(control_1_states), .BEGIN(xor_1_out), .END(datapath_1_end), .LSB(datapath_1_lsb),
    .clr(control_1_clr), .sM(control_1_sm), .L_M(control_1_l_m), .ALU(control_1_alu),
    .count(control_1_count), .CLK(CLK_out), .L_Q(control_1_l_q), .L_P(control_1_l_p), .RESTART(button_1_out),
    .Res_Clr(control_1_res_clr));
  Datapath datapath_1 (
    .Q(M_cand), .M(M_lier), .L_M(control_1_l_m), .clr(control_1_clr), .ALU(control_1_alu),
    .carry(Product_Carry), .clk(CLK_out), .sM(control_1_sm), .lsb(datapath_1_lsb), .END(datapath_1_end),
    .count(control_1_count), .M_2(M_lier_Second_Half), .P(Product_First_Half), .L_Q(control_1_l_q),
    .L_P(control_1_l_p), .Res_Clr(control_1_res_clr));
  // Probe on M_lier_Second_Half
  // Probe on control_1_states

  // Other names for the same wires on the sheet: M[31:0] = M_lier_Second_Half; P[31:0] = Product_First_Half

  // Notes on the sheet:
  //   MULT
  //   This Button Calculates Mult Again
  //   BEGIN
  //   BEGIN = Contstant 1 ==> provides used to process multiple time
  //   ==> PRESS MULT AFTER ENTERING THE MULTIPLICAND-MULTIPLIER NUMBERS! <==
  //   PRODUCT REGISTER
  //   AS TWO 32 BIT HALVES
  //   ===>  RESULT  <===
  //   Shows the current state.
  //   Shows the Carry of Product.
endmodule
