// Logisim project control.circ as structural Verilog: 1 circuit, main circuit Control
module Control (
  input  BEGIN,
  input  END,
  input  LSB,
  input  RESTART,
  input  CLK,
  output [2:0] STATES,
  output clr,
  output sM,
  output ALU,
  output count,
  output Res_Clr,
  output L_M,
  output L_Q,
  output L_P
);

  wire _3_out, and_1_out, and_2_out, and_3_out, and_4_out, and_5_out, and_6_out, and_7_out, and_8_out,
       and_9_out, N0, N1, N2;

  // Probe on {N2, N1, N0}
  Register #(.width(3)) register_1 (.D({N2, N1, N0}), .Q(STATES), .clk(CLK));  // open: en, clr
  // Probe on STATES
  and _0 (clr, ~STATES[0], ~STATES[1], ~STATES[2]);  // AND_Gate
  and and_1 (and_1_out, ~STATES[2], STATES[1], ~STATES[0], LSB);  // AND_Gate
  and and_2 (and_2_out, ~STATES[2], ~STATES[1], STATES[0]);  // AND_Gate
  or or_1 (N1, and_2_out, and_1_out, and_3_out);
  and and_3 (and_3_out, STATES[2], ~STATES[1], ~STATES[0], ~END);  // AND_Gate
  and and_4 (and_4_out, ~STATES[0], ~STATES[1], ~STATES[2], BEGIN, ~END);  // AND_Gate
  or or_2 (N0, and_9_out, and_4_out, and_5_out, and_6_out);
  and _3 (_3_out, ~STATES[2], STATES[1], STATES[0]);  // AND_Gate
  or or_3 (L_M, ALU, L_Q);
  and and_5 (and_5_out, ~STATES[2], STATES[1], ~STATES[0], LSB, ~END);  // AND_Gate
  and and_6 (and_6_out, STATES[2], ~STATES[1], ~STATES[0], END);  // AND_Gate
  and _1 (L_Q, ~STATES[2], ~STATES[1], STATES[0]);  // AND_Gate
  and _4 (ALU, STATES[2], ~STATES[1], ~STATES[0]);  // AND_Gate
  or or_4 (L_P, L_Q, _3_out, ALU);
  and and_7 (and_7_out, ~STATES[2], STATES[1], ~STATES[0], ~LSB);  // AND_Gate
  or or_5 (N2, and_6_out, and_7_out, and_8_out, and_9_out);
  and and_8 (and_8_out, ~STATES[2], STATES[1], STATES[0]);  // AND_Gate
  and and_9 (and_9_out, STATES[2], ~STATES[1], STATES[0], ~RESTART);  // AND_Gate

  assign count = ALU;
  assign Res_Clr = RESTART;
  assign sM = ALU;

  // Other names for the same wires on the sheet: RESTART_CLR = RESTART

  // Notes on the sheet:
  //   N
  //   P
  //   ===================================================================================
  //   P2-P1-P0
endmodule
